# Fritzing sketch ESP32MQTT433BridgeDog (saved by Fritzing 0.9.3b)
breadboards: 1
stripboards: 1

parts:
  R1 = Rotary Potentiometer (Small) [maximum_resistance=100kΩ package=THT]
  LED1 = smd LED [color="Red (633nm)" package="0603 [SMD]"]
  R2 = Resistor [tolerance=±5% resistance=330 package=THT]
  DHT22 = Humidity and Temperature Sensor RHT03 [part_number=TEMP/HUM]
  R3 = Resistor [tolerance=±5% resistance=10k package=THT]
  J3 = ESP32 DEVKITV1 LHS - 15 pins [form="♀ (female)" package=THT]  # not connected
  J5 = ESP32 DEVKITV1 RHS - 15 pins [form="♀ (female)" package=THT]  # not connected
  OLED_128_x_64 = Grove OLED 128x96

nets:
  VCC: R1.leg1, DHT22.Vcc, R3.Pin_0, OLED_128_x_64.VCC
  N1: R1.leg2, R2.Pin_0, DHT22.GND_2, OLED_128_x_64.GND
  N2: LED1.cathode, R2.Pin_1
  N3: DHT22.Data-signal, R3.Pin_1

notes:
  ESP32
  GPIO 36
  (ADC 0)
  GPIO 23
  (DHT22)
  SDA GPIO 21
  SCL GPIO 22
